# Fritzing sketch EspressoGuide (saved by Fritzing 0.9.2b)
stripboards: 1

parts:
  R1 = Resistor [tolerance=±5% resistance=220 package=THT]
  MV1 = MicroView [part_number=MicroView package="16pin wide"]
  Update_IF = female pin header, 5 pins [form="♀ (female)"]
  D1 = Rectifier Diode [part_number=1N4001 package="300 mil [THT]"]
  C1 = Ceramic Capacitor [capacitance=100nF package="100 mil [THT, multilayer]"]
  Power = female pin header, 2 pins [form="♀ (female)"]
  D2 = Rectifier Diode [part_number=1N4001 package="300 mil [THT]"]
  T1 = female pin header, 3 pins [form="♀ (female)"]
  C2 = Ceramic Capacitor [capacitance=100nF package="100 mil [THT, multilayer]"]
  D3 = Rectifier Diode [part_number=1N4001 package="300 mil [THT]"]
  D4 = Rectifier Diode [part_number=1N4001 package="300 mil [THT]"]
  D5 = Rectifier Diode [part_number=1N4001 package="300 mil [THT]"]
  Current_Sensor = female pin header, 2 pins [form="♀ (female)"]
  D6 = Rectifier Diode [part_number=1N4001 package="300 mil [THT]"]
  R3 = Resistor [tolerance=±5% resistance=220 package=THT]
  R2 = Resistor [tolerance=±5% resistance=4.7k package=THT]
  T2 = female pin header, 3 pins [form="♀ (female)"]
  SSR = female pin header, 2 pins [form="♀ (female)"]
  C3 = Electrolytic Capacitor [capacitance=47µF package="100 mil [THT, electrolytic]"]

nets (from the schematic view):
  N1: R1.Pin_0, MV1.D2, C2.0
  N2: R1.Pin_1, T1.pin1, T2.pin1
  N3: MV1.RESET, C1.0
  N4: MV1.A1, SSR.pin1
  N5: MV1.A0, R3.Pin_1
  N6: MV1.GND, Update_IF.pin2, Power.pin2, T1.pin3, C2.1, D3.anode, D4.anode, R2.Pin_1, T2.pin3, SSR.pin2, C3.-
  N7: MV1.RXD, Update_IF.pin4
  N8: MV1.TXD, Update_IF.pin3
  N9: MV1.D3, T1.pin2
  N10: MV1.D5, T2.pin2
  N11: MV1.Vin, D1.cathode, D2.cathode
  N12: Update_IF.pin1, D1.anode
  N13: Update_IF.pin5, C1.1
  N14: Power.pin1, D2.anode
  N15: D3.cathode, D5.anode, Current_Sensor.pin1
  N16: D4.cathode, Current_Sensor.pin2, D6.anode
  N17: D5.cathode, D6.cathode, R3.Pin_0, R2.Pin_0, C3.+

custom parts:
  MicroView: MicroView - Chip-sized Arduino with OLED display.
